// Logisim project sqrt2.circ as structural Verilog: 27 circuits, main circuit main
module main (
  input  ENABLE,
  input  [15:0] IO_DATA_IN,
  output NAN,
  output PINF,
  output NINF,
  output RESULT,
  output [15:0] IO_DATA_OUT
);

  wire CLK_out;

  Clock CLK (.out(CLK_out));
  sqrt sqrt_1 (
    .CLK(CLK_out), .ENABLE(ENABLE), .IO_DATA_IN(IO_DATA_IN), .IS_NAN(NAN), .IS_PINF(PINF), .IS_NINF(NINF),
    .RESULT(RESULT), .IO_DATA_OUT(IO_DATA_OUT));
endmodule

module sqrt (
  input  CLK,
  input  ENABLE,
  input  [15:0] IO_DATA_IN,
  output IS_NAN,
  output IS_PINF,
  output IS_NINF,
  output RESULT,
  output [15:0] IO_DATA_OUT
);

  wire and_1_out, is_neg_num_1_res, is_neg_zero_1_res, is_pos_zero_1_res, it_is_nan_1_res, not_2_out,
       not_3_out, not_4_out, not_5_out, not_6_out, num1_greater_equals_num2_1_equal,
       num1_greater_equals_num2_2_equal, num1_greater_equals_num2_3_equal, num1_greater_equals_num2_4_equal,
       num1_greater_equals_num2_4_greater, or_3_out;
  wire [4:0] normalization_mant_1_res_exp, parsing_1_exp;
  wire [6:0] undriven;
  wire [9:0] parsing_1_mant;
  wire [11:0] bit_extender_1_out, borrow_read_out_num, borrow_write_out_num, counter_1_value_16bit,
       if_12bit_1_result, if_12bit_2_result, if_12bit_3_result, memory_1_out_num, memory_2_out_num,
       memory_3_out_num, normalization_mant_1_mant_12bit, res_read_out_num, res_write_out_num,
       shift_12bit_1_res_12bit, shift_12bit_2_res_12bit, shift_12bit_3_res_12bit, shift_12bit_4_res_12bit,
       shift_12bit_5_res_12bit, substractor_1_res_12bit, summator_1_res_12bit, summator_2_res_12bit;
  wire [15:0] not_1_out, quite_nan_1_qnan, transistor_1_out;
  wire [15:15] parsing_1_sign;

  Transistor #(.width(16)) transistor_1 (.in(IO_DATA_IN), .out(transistor_1_out), .gate(not_1_out));
  counter counter_1 (.C(CLK), .enable(ENABLE), .value_16bit(counter_1_value_16bit));
  Num1_greater_equals_Num2 num1_greater_equals_num2_1 (
    .Num1(counter_1_value_16bit), .Num2(12'h1), .equal(num1_greater_equals_num2_1_equal));  // open: greater
  not not_1 (not_1_out[0], num1_greater_equals_num2_1_equal);
  parsing parsing_1 (.num(transistor_1_out), .mant(parsing_1_mant), .exp(parsing_1_exp), .sign(parsing_1_sign[15]));
  not not_2 (not_2_out, not_1_out[0]);
  normalization_mant normalization_mant_1 (
    .exp(parsing_1_exp), .mant_10bit(parsing_1_mant), .res_exp(normalization_mant_1_res_exp),
    .mant_12bit(normalization_mant_1_mant_12bit));
  is_pos_inf is_pos_inf_1 (.sign(parsing_1_sign[15]), .exp(parsing_1_exp), .mant(parsing_1_mant), .res(IS_PINF));
  is_pos_zero is_pos_zero_1 (
    .sign(parsing_1_sign[15]), .exp(parsing_1_exp), .mant(parsing_1_mant), .res(is_pos_zero_1_res));
  is_neg_zero is_neg_zero_1 (
    .sign(parsing_1_sign[15]), .exp(parsing_1_exp), .mant(parsing_1_mant), .res(is_neg_zero_1_res));
  it_is_NaN it_is_nan_1 (.exp(parsing_1_exp), .mant(parsing_1_mant), .res(it_is_nan_1_res));
  is_neg_num is_neg_num_1 (
    .sign(parsing_1_sign[15]), .exp(parsing_1_exp), .mant(parsing_1_mant), .res(is_neg_num_1_res));
  if_12bit if_12bit_1 (
    .Value_1(normalization_mant_1_mant_12bit), .expression(not_2_out), .Value_2(memory_3_out_num),
    .result(if_12bit_1_result));
  or or_1 (RESULT, IS_PINF, is_pos_zero_1_res, is_neg_zero_1_res, it_is_nan_1_res, is_neg_num_1_res);
  quite_Nan quite_nan_1 (.QNAN(quite_nan_1_qnan));
  not not_3 (not_3_out, not_1_out[0]);
  or or_2 (IS_NAN, it_is_nan_1_res, is_neg_num_1_res);
  not not_4 (not_4_out, CLK);
  if_16bit if_16bit_1 (
    .Value_1(quite_nan_1_qnan), .expression(is_neg_num_1_res),
    .Value_2({parsing_1_sign[15], parsing_1_exp, parsing_1_mant}));  // open: result
  // Probe on memory_1_out_num
  memory memory_1 (
    .number({undriven, normalization_mant_1_res_exp}), .c(not_3_out), .enable(ENABLE),
    .out_num(memory_1_out_num));
  memory memory_2 (.number(if_12bit_1_result), .c(CLK), .enable(ENABLE), .out_num(memory_2_out_num));
  memory memory_3 (.number(shift_12bit_2_res_12bit), .c(not_4_out), .enable(ENABLE), .out_num(memory_3_out_num));
  // Probe on memory_2_out_num
  shift_12bit shift_12bit_1 (.num_12bit(memory_2_out_num), .res_12bit(shift_12bit_1_res_12bit));
  shift_12bit shift_12bit_2 (.num_12bit(shift_12bit_1_res_12bit), .res_12bit(shift_12bit_2_res_12bit));
  not not_5 (not_5_out, CLK);
  not not_6 (not_6_out, CLK);
  memory res_read (.number(res_write_out_num), .c(CLK), .enable(ENABLE), .out_num(res_read_out_num));
  memory res_write (.number(if_12bit_2_result), .c(not_5_out), .enable(ENABLE), .out_num(res_write_out_num));
  memory borrow_read (.number(borrow_write_out_num), .c(CLK), .enable(ENABLE), .out_num(borrow_read_out_num));
  memory borrow_write (.number(if_12bit_3_result), .c(not_6_out), .enable(ENABLE), .out_num(borrow_write_out_num));
  // Probe on res_write_out_num
  // Probe on borrow_write_out_num
  shift_12bit shift_12bit_3 (.num_12bit(res_read_out_num), .res_12bit(shift_12bit_3_res_12bit));
  shift_12bit shift_12bit_4 (.num_12bit(borrow_read_out_num), .res_12bit(shift_12bit_4_res_12bit));
  Num1_greater_equals_Num2 num1_greater_equals_num2_2 (
    .Num1(borrow_read_out_num), .Num2({12{1'b0}}), .equal(num1_greater_equals_num2_2_equal));  // open: greater
  Num1_greater_equals_Num2 num1_greater_equals_num2_3 (
    .Num1(memory_2_out_num), .Num2({12{1'b0}}), .equal(num1_greater_equals_num2_3_equal));  // open: greater
  assign bit_extender_1_out = {{10{1'b0}}, memory_2_out_num[11:10]};  // Bit_Extender bit_extender_1
  shift_12bit shift_12bit_5 (.num_12bit(shift_12bit_4_res_12bit), .res_12bit(shift_12bit_5_res_12bit));
  and and_1 (and_1_out, num1_greater_equals_num2_2_equal, num1_greater_equals_num2_3_equal);
  // Probe on and_1_out
  summator summator_1 (.num1(shift_12bit_3_res_12bit), .num2(12'h1), .res_12bit(summator_1_res_12bit));
  summator summator_2 (.num1(bit_extender_1_out), .num2(shift_12bit_5_res_12bit), .res_12bit(summator_2_res_12bit));
  Num1_greater_equals_Num2 num1_greater_equals_num2_4 (
    .Num1(summator_2_res_12bit), .Num2(summator_1_res_12bit), .greater(num1_greater_equals_num2_4_greater),
    .equal(num1_greater_equals_num2_4_equal));
  substractor substractor_1 (
    .X_12bit(summator_2_res_12bit), .Y_12bit(summator_1_res_12bit), .res_12bit(substractor_1_res_12bit));
  or or_3 (or_3_out, num1_greater_equals_num2_4_greater, num1_greater_equals_num2_4_equal);
  if_12bit if_12bit_2 (
    .Value_1(summator_1_res_12bit), .expression(or_3_out), .Value_2(shift_12bit_3_res_12bit),
    .result(if_12bit_2_result));
  if_12bit if_12bit_3 (
    .Value_1(substractor_1_res_12bit), .expression(or_3_out), .Value_2(summator_2_res_12bit),
    .result(if_12bit_3_result));
  // Pins of 1 and 16 bits meet at not_1_out

  assign IO_DATA_OUT = IO_DATA_IN;
  assign IS_NINF = 1'b0;
endmodule

module shift_12bit (
  input  [11:0] num_12bit,
  output [11:0] res_12bit
);


  assign res_12bit = {num_12bit[10:0], 1'b0};
endmodule

module full_substracter (
  input  X,
  input  Y,
  input  B_in,
  output D,
  output B_out
);

  wire and_1_out, and_2_out, not_1_out, not_2_out, xor_1_out;

  xor xor_1 (xor_1_out, X, Y);
  not not_1 (not_1_out, X);
  and and_1 (and_1_out, not_1_out, Y);
  not not_2 (not_2_out, xor_1_out);
  xor xor_2 (D, xor_1_out, B_in);
  and and_2 (and_2_out, B_in, not_2_out);
  or or_1 (B_out, and_2_out, and_1_out);
endmodule

module hulf_substracter (
  input  X,
  input  Y,
  output difference,
  output borrow
);

  wire nand_1_out, nand_2_out, nand_3_out;

  nand nand_1 (nand_1_out, X, Y);
  nand nand_2 (nand_2_out, X, nand_1_out);
  nand nand_3 (nand_3_out, nand_1_out, Y);
  nand nand_4 (difference, nand_2_out, nand_3_out);
  nand nand_5 (borrow, nand_3_out, nand_3_out);
endmodule

module substractor (
  input  [11:0] X_12bit,
  input  [11:0] Y_12bit,
  output [11:0] res_12bit
);

  wire full_substracter_1_b_out, full_substracter_2_b_out, full_substracter_3_b_out,
       full_substracter_4_b_out, full_substracter_5_b_out, full_substracter_6_b_out,
       full_substracter_7_b_out, full_substracter_8_b_out, full_substracter_9_b_out,
       full_substracter_10_b_out, full_substracter_11_b_out;

  full_substracter full_substracter_1 (
    .X(X_12bit[0]), .Y(Y_12bit[0]), .B_in(1'b0), .D(res_12bit[0]), .B_out(full_substracter_1_b_out));
  full_substracter full_substracter_2 (
    .X(X_12bit[1]), .Y(Y_12bit[1]), .B_in(full_substracter_1_b_out), .D(res_12bit[1]),
    .B_out(full_substracter_2_b_out));
  full_substracter full_substracter_3 (
    .X(X_12bit[2]), .Y(Y_12bit[2]), .B_in(full_substracter_2_b_out), .D(res_12bit[2]),
    .B_out(full_substracter_3_b_out));
  full_substracter full_substracter_4 (
    .X(X_12bit[3]), .Y(Y_12bit[3]), .B_in(full_substracter_3_b_out), .D(res_12bit[3]),
    .B_out(full_substracter_4_b_out));
  full_substracter full_substracter_5 (
    .X(X_12bit[4]), .Y(Y_12bit[4]), .B_in(full_substracter_4_b_out), .D(res_12bit[4]),
    .B_out(full_substracter_5_b_out));
  full_substracter full_substracter_6 (
    .X(X_12bit[5]), .Y(Y_12bit[5]), .B_in(full_substracter_5_b_out), .D(res_12bit[5]),
    .B_out(full_substracter_6_b_out));
  full_substracter full_substracter_7 (
    .X(X_12bit[6]), .Y(Y_12bit[6]), .B_in(full_substracter_6_b_out), .D(res_12bit[6]),
    .B_out(full_substracter_7_b_out));
  full_substracter full_substracter_8 (
    .X(X_12bit[7]), .Y(Y_12bit[7]), .B_in(full_substracter_7_b_out), .D(res_12bit[7]),
    .B_out(full_substracter_8_b_out));
  full_substracter full_substracter_9 (
    .X(X_12bit[8]), .Y(Y_12bit[8]), .B_in(full_substracter_8_b_out), .D(res_12bit[8]),
    .B_out(full_substracter_9_b_out));
  full_substracter full_substracter_10 (
    .X(X_12bit[9]), .Y(Y_12bit[9]), .B_in(full_substracter_9_b_out), .D(res_12bit[9]),
    .B_out(full_substracter_10_b_out));
  full_substracter full_substracter_11 (
    .X(X_12bit[10]), .Y(Y_12bit[10]), .B_in(full_substracter_10_b_out), .D(res_12bit[10]),
    .B_out(full_substracter_11_b_out));
  full_substracter full_substracter_12 (
    .X(X_12bit[11]), .Y(Y_12bit[11]), .B_in(full_substracter_11_b_out), .D(res_12bit[11]));  // open: B_out
endmodule

module Num1_greater_equals_Num2 (
  input  [11:0] Num1,
  input  [11:0] Num2,
  output greater,
  output equal
);

  wire comporator_2_equal, comporator_2_greater, comporator_3_equal, comporator_3_greater,
       comporator_4_equal, comporator_4_greater, comporator_5_equal, comporator_5_greater,
       comporator_6_equal, comporator_6_greater, comporator_7_equal, comporator_7_greater,
       comporator_8_equal, comporator_8_greater, comporator_9_equal, comporator_9_greater,
       comporator_10_equal, comporator_10_greater, comporator_11_equal, comporator_11_greater,
       comporator_12_equal, comporator_12_greater;

  comporator comporator_1 (
    .Bit_1(Num1[0]), .Bit_2(Num2[0]), .prev_gt(comporator_2_greater), .prev_eq(comporator_2_equal),
    .greater(greater), .equal(equal));
  comporator comporator_2 (
    .Bit_1(Num1[1]), .Bit_2(Num2[1]), .prev_gt(comporator_3_greater), .prev_eq(comporator_3_equal),
    .greater(comporator_2_greater), .equal(comporator_2_equal));
  comporator comporator_3 (
    .Bit_1(Num1[2]), .Bit_2(Num2[2]), .prev_gt(comporator_4_greater), .prev_eq(comporator_4_equal),
    .greater(comporator_3_greater), .equal(comporator_3_equal));
  comporator comporator_4 (
    .Bit_1(Num1[3]), .Bit_2(Num2[3]), .prev_gt(comporator_5_greater), .prev_eq(comporator_5_equal),
    .greater(comporator_4_greater), .equal(comporator_4_equal));
  comporator comporator_5 (
    .Bit_1(Num1[4]), .Bit_2(Num2[4]), .prev_gt(comporator_6_greater), .prev_eq(comporator_6_equal),
    .greater(comporator_5_greater), .equal(comporator_5_equal));
  comporator comporator_6 (
    .Bit_1(Num1[5]), .Bit_2(Num2[5]), .prev_gt(comporator_7_greater), .prev_eq(comporator_7_equal),
    .greater(comporator_6_greater), .equal(comporator_6_equal));
  comporator comporator_7 (
    .Bit_1(Num1[6]), .Bit_2(Num2[6]), .prev_gt(comporator_8_greater), .prev_eq(comporator_8_equal),
    .greater(comporator_7_greater), .equal(comporator_7_equal));
  comporator comporator_8 (
    .Bit_1(Num1[7]), .Bit_2(Num2[7]), .prev_gt(comporator_9_greater), .prev_eq(comporator_9_equal),
    .greater(comporator_8_greater), .equal(comporator_8_equal));
  comporator comporator_9 (
    .Bit_1(Num1[8]), .Bit_2(Num2[8]), .prev_gt(comporator_10_greater), .prev_eq(comporator_10_equal),
    .greater(comporator_9_greater), .equal(comporator_9_equal));
  comporator comporator_10 (
    .Bit_1(Num1[9]), .Bit_2(Num2[9]), .prev_gt(comporator_11_greater), .prev_eq(comporator_11_equal),
    .greater(comporator_10_greater), .equal(comporator_10_equal));
  comporator comporator_11 (
    .Bit_1(Num1[10]), .Bit_2(Num2[10]), .prev_gt(comporator_12_greater), .prev_eq(comporator_12_equal),
    .greater(comporator_11_greater), .equal(comporator_11_equal));
  comporator comporator_12 (
    .Bit_1(Num1[11]), .Bit_2(Num2[11]), .prev_gt(1'b0), .prev_eq(1'b1), .greater(comporator_12_greater),
    .equal(comporator_12_equal));
endmodule

module comporator (
  input  Bit_1,
  input  Bit_2,
  input  prev_gt,
  input  prev_eq,
  output greater,
  output equal
);

  wire and_1_out, not_1_out, xnor_1_out;

  not not_1 (not_1_out, Bit_2);
  xnor xnor_1 (xnor_1_out, Bit_1, Bit_2);
  and and_1 (and_1_out, Bit_1, not_1_out, prev_eq);
  or or_1 (greater, and_1_out, prev_gt);
  and and_2 (equal, xnor_1_out, prev_eq);
endmodule

module D_trigger (
  input  C,
  input  D,
  input  enable,
  output Q,
  output not_Q
);

  wire not_1_out;

  not not_1 (not_1_out, D);
  RSC_trigger rsc_trigger_1 (.R(not_1_out), .C(C), .S(D), .enable(enable), .Q(Q), .not_Q(not_Q));
endmodule

module RS_trigger (
  input  R,
  input  S,
  input  enable,
  output Q,
  output not_Q
);

  wire nor_2_out, not_1_out, or_1_out, por_1_out;

  not not_1 (not_1_out, enable);
  POR por_1 (.out(por_1_out));
  nor nor_1 (Q, R, not_Q);
  nor nor_2 (nor_2_out, Q, S);
  or or_1 (or_1_out, not_1_out, por_1_out);
  or or_2 (not_Q, nor_2_out, or_1_out);
endmodule

module summator (
  input  [11:0] num1,
  input  [11:0] num2,
  output [11:0] res_12bit
);

  wire sum_bit_1_carry_out, sum_bit_2_carry_out, sum_bit_3_carry_out, sum_bit_4_carry_out,
       sum_bit_5_carry_out, sum_bit_6_carry_out, sum_bit_7_carry_out, sum_bit_8_carry_out,
       sum_bit_9_carry_out, sum_bit_10_carry_out, sum_bit_11_carry_out;

  sum_bit sum_bit_1 (
    .carry_in(1'b0), .bit_1(num1[0]), .bit_2(num2[0]), .res(res_12bit[0]), .carry_out(sum_bit_1_carry_out));
  sum_bit sum_bit_2 (
    .carry_in(sum_bit_1_carry_out), .bit_1(num1[1]), .bit_2(num2[1]), .res(res_12bit[1]),
    .carry_out(sum_bit_2_carry_out));
  sum_bit sum_bit_3 (
    .carry_in(sum_bit_2_carry_out), .bit_1(num1[2]), .bit_2(num2[2]), .res(res_12bit[2]),
    .carry_out(sum_bit_3_carry_out));
  sum_bit sum_bit_4 (
    .carry_in(sum_bit_3_carry_out), .bit_1(num1[3]), .bit_2(num2[3]), .res(res_12bit[3]),
    .carry_out(sum_bit_4_carry_out));
  sum_bit sum_bit_5 (
    .carry_in(sum_bit_4_carry_out), .bit_1(num1[4]), .bit_2(num2[4]), .res(res_12bit[4]),
    .carry_out(sum_bit_5_carry_out));
  sum_bit sum_bit_6 (
    .carry_in(sum_bit_5_carry_out), .bit_1(num1[5]), .bit_2(num2[5]), .res(res_12bit[5]),
    .carry_out(sum_bit_6_carry_out));
  sum_bit sum_bit_7 (
    .carry_in(sum_bit_6_carry_out), .bit_1(num1[6]), .bit_2(num2[6]), .res(res_12bit[6]),
    .carry_out(sum_bit_7_carry_out));
  sum_bit sum_bit_8 (
    .carry_in(sum_bit_7_carry_out), .bit_1(num1[7]), .bit_2(num1[8]), .res(res_12bit[7]),
    .carry_out(sum_bit_8_carry_out));
  sum_bit sum_bit_9 (
    .carry_in(sum_bit_8_carry_out), .bit_1(num1[8]), .bit_2(num2[8]), .res(res_12bit[8]),
    .carry_out(sum_bit_9_carry_out));
  sum_bit sum_bit_10 (
    .carry_in(sum_bit_9_carry_out), .bit_1(num1[9]), .bit_2(num2[9]), .res(res_12bit[9]),
    .carry_out(sum_bit_10_carry_out));
  sum_bit sum_bit_11 (
    .carry_in(sum_bit_10_carry_out), .bit_1(num1[10]), .bit_2(num2[10]), .res(res_12bit[10]),
    .carry_out(sum_bit_11_carry_out));
  sum_bit sum_bit_12 (
    .carry_in(sum_bit_11_carry_out), .bit_1(num1[11]), .bit_2(num2[11]), .res(res_12bit[11]));  // open: carry_out

  assign num2[7] = num1[8];
endmodule

module sum_bit (
  input  carry_in,
  input  bit_1,
  input  bit_2,
  output res,
  output carry_out
);

  wire and_1_out, and_2_out, xor_1_out;

  xor xor_1 (xor_1_out, bit_1, bit_2);
  and and_1 (and_1_out, bit_1, bit_2);
  xor xor_2 (res, carry_in, xor_1_out);
  and and_2 (and_2_out, carry_in, xor_1_out);
  or or_1 (carry_out, and_2_out, and_1_out);
endmodule

module RSC_trigger (
  input  R,
  input  C,
  input  S,
  input  enable,
  output Q,
  output not_Q
);

  wire and_1_out, and_2_out;

  and and_1 (and_1_out, R, C);
  and and_2 (and_2_out, C, S);
  RS_trigger rs_trigger_1 (.R(and_1_out), .S(and_2_out), .enable(enable), .Q(Q), .not_Q(not_Q));
endmodule

module memory (
  input  [11:0] number,
  input  c,
  input  enable,
  output [11:0] out_num
);

  D_trigger d_trigger_1 (.C(c), .D(number[0]), .enable(enable), .Q(out_num[0]));  // open: not_Q
  D_trigger d_trigger_2 (.C(c), .D(number[1]), .enable(enable), .Q(out_num[1]));  // open: not_Q
  D_trigger d_trigger_3 (.C(c), .D(number[2]), .enable(enable), .Q(out_num[2]));  // open: not_Q
  D_trigger d_trigger_4 (.C(c), .D(number[3]), .enable(enable), .Q(out_num[3]));  // open: not_Q
  D_trigger d_trigger_5 (.C(c), .D(number[4]), .enable(enable), .Q(out_num[4]));  // open: not_Q
  D_trigger d_trigger_6 (.C(c), .D(number[5]), .enable(enable), .Q(out_num[5]));  // open: not_Q
  D_trigger d_trigger_7 (.C(c), .D(number[6]), .enable(enable), .Q(out_num[6]));  // open: not_Q
  D_trigger d_trigger_8 (.C(c), .D(number[7]), .enable(enable), .Q(out_num[7]));  // open: not_Q
  D_trigger d_trigger_9 (.C(c), .D(number[8]), .enable(enable), .Q(out_num[8]));  // open: not_Q
  D_trigger d_trigger_10 (.C(c), .D(number[9]), .enable(enable), .Q(out_num[9]));  // open: not_Q
  D_trigger d_trigger_11 (.C(c), .D(number[10]), .enable(enable), .Q(out_num[10]));  // open: not_Q
  D_trigger d_trigger_12 (.C(c), .D(number[11]), .enable(enable), .Q(out_num[11]));  // open: not_Q
endmodule

module parsing (
  input  [15:0] num,
  output [9:0] mant,
  output [4:0] exp,
  output sign
);


  assign exp = num[14:10];
  assign mant = num[9:0];
  assign sign = num[15];
endmodule

module is_pos_inf (
  input  sign,
  input  [4:0] exp,
  input  [9:0] mant,
  output res
);

  wire not_1_out, num1_greater_equals_num2_1_equal, num1_greater_equals_num2_2_equal;
  wire [1:0] undriven;
  wire [6:0] undriven_2;

  not not_1 (not_1_out, sign);
  Num1_greater_equals_Num2 num1_greater_equals_num2_1 (
    .Num1({undriven_2, exp}), .Num2(12'h1f), .equal(num1_greater_equals_num2_1_equal));  // open: greater
  Num1_greater_equals_Num2 num1_greater_equals_num2_2 (
    .Num1({undriven, mant}), .Num2({12{1'b0}}), .equal(num1_greater_equals_num2_2_equal));  // open: greater
  and and_1 (res, not_1_out, num1_greater_equals_num2_1_equal, num1_greater_equals_num2_2_equal);
endmodule

module is_pos_zero (
  input  sign,
  input  [4:0] exp,
  input  [9:0] mant,
  output res
);

  wire not_1_out, num1_greater_equals_num2_1_equal, num1_greater_equals_num2_2_equal;
  wire [1:0] undriven;
  wire [6:0] undriven_2;

  not not_1 (not_1_out, sign);
  Num1_greater_equals_Num2 num1_greater_equals_num2_1 (
    .Num1({undriven_2, exp}), .Num2({12{1'b0}}), .equal(num1_greater_equals_num2_1_equal));  // open: greater
  Num1_greater_equals_Num2 num1_greater_equals_num2_2 (
    .Num1({undriven, mant}), .Num2({12{1'b0}}), .equal(num1_greater_equals_num2_2_equal));  // open: greater
  and and_1 (res, not_1_out, num1_greater_equals_num2_1_equal, num1_greater_equals_num2_2_equal);
endmodule

module is_neg_zero (
  input  sign,
  input  [4:0] exp,
  input  [9:0] mant,
  output res
);

  wire num1_greater_equals_num2_1_equal, num1_greater_equals_num2_2_equal;
  wire [1:0] undriven;
  wire [6:0] undriven_2;

  Num1_greater_equals_Num2 num1_greater_equals_num2_1 (
    .Num1({undriven_2, exp}), .Num2({12{1'b0}}), .equal(num1_greater_equals_num2_1_equal));  // open: greater
  Num1_greater_equals_Num2 num1_greater_equals_num2_2 (
    .Num1({undriven, mant}), .Num2({12{1'b0}}), .equal(num1_greater_equals_num2_2_equal));  // open: greater
  and and_1 (res, sign, num1_greater_equals_num2_1_equal, num1_greater_equals_num2_2_equal);
endmodule

module quite_Nan (
  output [15:0] QNAN
);


  assign QNAN = 16'hfe00;
endmodule

module it_is_NaN (
  input  [4:0] exp,
  input  [9:0] mant,
  output res
);

  wire not_1_out, num1_greater_equals_num2_1_equal, num1_greater_equals_num2_2_equal;
  wire [1:0] undriven;
  wire [6:0] undriven_2;

  Num1_greater_equals_Num2 num1_greater_equals_num2_1 (
    .Num1({undriven_2, exp}), .Num2(12'h1f), .equal(num1_greater_equals_num2_1_equal));  // open: greater
  Num1_greater_equals_Num2 num1_greater_equals_num2_2 (
    .Num1({undriven, mant}), .Num2({12{1'b0}}), .equal(num1_greater_equals_num2_2_equal));  // open: greater
  not not_1 (not_1_out, num1_greater_equals_num2_2_equal);
  and and_1 (res, num1_greater_equals_num2_1_equal, not_1_out);
endmodule

module is_neg_num (
  input  sign,
  input  [4:0] exp,
  input  [9:0] mant,
  output res
);

  wire is_neg_zero_1_res, it_is_nan_1_res, not_1_out, not_2_out;

  is_neg_zero is_neg_zero_1 (.sign(sign), .exp(exp), .mant(mant), .res(is_neg_zero_1_res));
  it_is_NaN it_is_nan_1 (.exp(exp), .mant(mant), .res(it_is_nan_1_res));
  not not_1 (not_1_out, is_neg_zero_1_res);
  not not_2 (not_2_out, it_is_nan_1_res);
  and and_1 (res, sign, not_1_out, not_2_out);
endmodule

module if_16bit (
  input  [15:0] Value_1,
  input  expression,
  input  [15:0] Value_2,
  output [15:0] result
);

  wire not_1_out;

  not not_1 (not_1_out, expression);
  Transistor #(.\type ("n"), .width(16)) transistor_1 (.in(Value_1), .out(result), .gate(expression));
  Transistor #(.\type ("n"), .width(16)) transistor_2 (.in(Value_2), .out(result), .gate(not_1_out));
  Pull_Resistor #(.pull(1)) pull_resistor_1 (.node(result));
endmodule

module normalization_mant (
  input  [4:0] exp,
  input  [9:0] mant_10bit,
  output [4:0] res_exp,
  output [11:0] mant_12bit
);

  wire [3:0] if_16bit_1_result, undriven_3, undriven_4, undriven_5;
  wire [6:0] undriven;
  wire [10:0] undriven_2;
  wire [11:0] shift_12bit_1_res_12bit, substractor_1_res_12bit;
  wire [15:5] if_16bit_2_result;

  substractor substractor_1 (.X_12bit({undriven, exp}), .Y_12bit(12'h1), .res_12bit(substractor_1_res_12bit));
  shift_12bit shift_12bit_1 (.num_12bit({2'b01, mant_10bit}), .res_12bit(shift_12bit_1_res_12bit));
  if_16bit if_16bit_1 (
    .Value_1({undriven_3, 2'b01, mant_10bit}), .expression(exp[0]),
    .Value_2({undriven_4, shift_12bit_1_res_12bit}), .result({if_16bit_1_result, mant_12bit}));
  if_16bit if_16bit_2 (
    .Value_1({undriven_2, exp}), .expression(exp[0]), .Value_2({undriven_5, substractor_1_res_12bit}),
    .result({if_16bit_2_result, res_exp}));
endmodule

module jk_trigger (
  input  K,
  input  C,
  input  J,
  input  enable,
  output Q,
  output not_Q
);

  wire and_1_out, and_2_out, not_1_out, rsc_trigger_1_not_q, rsc_trigger_1_q;

  and and_1 (and_1_out, Q, K);
  and and_2 (and_2_out, J, not_Q);
  not not_1 (not_1_out, C);
  RSC_trigger rsc_trigger_1 (
    .R(and_1_out), .C(C), .S(and_2_out), .enable(enable), .Q(rsc_trigger_1_q), .not_Q(rsc_trigger_1_not_q));
  RSC_trigger rsc_trigger_2 (
    .R(rsc_trigger_1_not_q), .C(not_1_out), .S(rsc_trigger_1_q), .enable(enable), .Q(Q), .not_Q(not_Q));
endmodule

module counter (
  input  C,
  input  enable,
  output [11:0] value_16bit
);

  wire jk_trigger_1_not_q, jk_trigger_2_not_q, jk_trigger_3_not_q, not_1_out, not_2_out, not_3_out, not_4_out;

  not not_1 (not_1_out, C);
  jk_trigger jk_trigger_1 (
    .K(1'b1), .C(not_1_out), .J(1'b1), .enable(enable), .Q(value_16bit[0]), .not_Q(jk_trigger_1_not_q));
  not not_2 (not_2_out, jk_trigger_1_not_q);
  jk_trigger jk_trigger_2 (
    .K(1'b1), .C(not_2_out), .J(1'b1), .enable(enable), .Q(value_16bit[1]), .not_Q(jk_trigger_2_not_q));
  not not_3 (not_3_out, jk_trigger_2_not_q);
  jk_trigger jk_trigger_3 (
    .K(1'b1), .C(not_3_out), .J(1'b1), .enable(enable), .Q(value_16bit[2]), .not_Q(jk_trigger_3_not_q));
  not not_4 (not_4_out, jk_trigger_3_not_q);
  jk_trigger jk_trigger_4 (.K(1'b1), .C(not_4_out), .J(1'b1), .enable(enable), .Q(value_16bit[3]));  // open: not_Q

  assign value_16bit[11:4] = {8{1'b0}};
endmodule

module test (
  input  in_1
);

  wire clock_1_out;
  wire [11:0] memory_1_out_num, summator_1_res_12bit;
  wire [15:0] if_16bit_1_result;

  Clock clock_1 (.out(clock_1_out));
  if_16bit if_16bit_1 (.Value_1({16{1'b0}}), .expression(clock_1_out), .Value_2(16'h1), .result(if_16bit_1_result));
  memory memory_1 (
    .number(summator_1_res_12bit), .c(if_16bit_1_result[0]), .enable(clock_1_out), .out_num(memory_1_out_num));
  summator summator_1 (.num1(memory_1_out_num), .num2(12'h1), .res_12bit(summator_1_res_12bit));
  // Probe on summator_1_res_12bit
endmodule

module if_12bit (
  input  [11:0] Value_1,
  input  expression,
  input  [11:0] Value_2,
  output [11:0] result
);

  wire not_1_out;

  not not_1 (not_1_out, expression);
  Transistor #(.\type ("n"), .width(12)) transistor_1 (.in(Value_1), .out(result), .gate(expression));
  Transistor #(.\type ("n"), .width(12)) transistor_2 (.in(Value_2), .out(result), .gate(not_1_out));
  Pull_Resistor #(.pull(1)) pull_resistor_1 (.node(result));
endmodule
